// Logisim project digital_prjct.circ as structural Verilog: 1 circuit, main circuit main
module main (
);

  wire adder_1_cout, and_1_out, and_2_out, clock_1_out, decoder_1_out1, decoder_1_out2, decoder_1_out3,
       decoder_2_out0, decoder_2_out1, decoder_2_out2, decoder_2_out3, decoder_2_out4, decoder_2_out5,
       decoder_2_out6, decoder_2_out7, decoder_2_out8, decoder_2_out9, decoder_2_out10, decoder_2_out11,
       decoder_2_out12, decoder_2_out13, decoder_2_out14, decoder_2_out15, not_1_out, or_1_out;
  wire [1:0] counter_1_q, or_3_out;
  wire [3:0] adder_1_out, counter_2_q, multiplexer_1_out, ram_1_dout, register_2_q, register_4_q,
       subtractor_1_out, undriven;
  wire [7:0] register_1_q, rom_1_data;

  Clock #(.phaseOffset(1)) clock_1 (.out(clock_1_out));
  Counter #(.max('h3), .width(2)) counter_1 (
    .up(1'b1), .count(1'b1), .clk(clock_1_out), .Q(counter_1_q));  // open: clr, load, D, carry
  not not_1 (not_1_out, clock_1_out);
  Decoder #(.select(2)) decoder_1 (
    .out1(decoder_1_out1), .out2(decoder_1_out2), .out3(decoder_1_out3), .sel(counter_1_q));  // open: out0, en
  Counter #(.max('hf), .width(4)) counter_2 (
    .up(1'b1), .count(decoder_1_out1), .clk(not_1_out), .Q(counter_2_q));  // open: clr, load, D, carry
  ROM #(.addrWidth(4)) rom_1 (.addr(counter_2_q), .data(rom_1_data));
  Register register_1 (.D(rom_1_data), .en(decoder_1_out1), .clk(clock_1_out), .Q(register_1_q));  // open: clr
  // Probe on register_1_q[3:0]
  // Probe on register_1_q[7:4]
  // Probe on register_1_q
  Decoder #(.select(4)) decoder_2 (
    .out0(decoder_2_out0), .out1(decoder_2_out1), .out2(decoder_2_out2), .out3(decoder_2_out3),
    .out4(decoder_2_out4), .out5(decoder_2_out5), .out6(decoder_2_out6), .out7(decoder_2_out7),
    .out8(decoder_2_out8), .out9(decoder_2_out9), .out10(decoder_2_out10), .out11(decoder_2_out11),
    .out12(decoder_2_out12), .out13(decoder_2_out13), .out14(decoder_2_out14), .out15(decoder_2_out15),
    .sel(register_1_q[7:4]));  // open: en
  // Probe on decoder_2_out0
  // Probe on decoder_2_out1
  // Probe on decoder_2_out2
  // Probe on decoder_2_out3
  // Probe on decoder_2_out4
  // Probe on decoder_2_out5
  // Probe on decoder_2_out10
  // Probe on decoder_2_out11
  // Probe on decoder_2_out12
  // Probe on decoder_2_out13
  // Probe on decoder_2_out14
  // Probe on decoder_2_out15
  // Probe on decoder_2_out6
  // Probe on decoder_2_out7
  // Probe on decoder_2_out8
  // Probe on decoder_2_out9
  // Probe on register_1_q[3:0]
  or or_1 (or_1_out, decoder_2_out1, decoder_2_out3, decoder_2_out4);
  RAM #(.addrWidth(4), .dataWidth(4), .trigger("high")) ram_1 (
    .addr(register_1_q[3:0]), .oe(and_1_out), .dout(ram_1_dout));  // open: we, din
  and and_1 (and_1_out, decoder_1_out2, or_1_out);
  Register #(.width(4)) register_2 (
    .D(multiplexer_1_out), .en(and_2_out), .clk(not_1_out), .Q(register_2_q));  // open: clr
  and and_2 (and_2_out, or_1_out, decoder_1_out3);
  // Probe on multiplexer_1_out
  // Probe on register_2_q
  or or_2 (or_3_out[1], decoder_2_out4, decoder_2_out1, decoder_2_out12);
  or or_3 (or_3_out[0], decoder_2_out1, decoder_2_out5, decoder_2_out6, decoder_2_out7, decoder_2_out8);
  Register #(.width(4)) register_3 (.D(register_1_q[3:0]), .en(decoder_2_out2), .clk(not_1_out));  // open: Q, clr
  Register #(.width(4)) register_4 (.D(ram_1_dout), .en(and_1_out), .clk(not_1_out), .Q(register_4_q));  // open: clr
  Adder #(.width(4)) adder_1 (.a(register_2_q), .b(register_4_q), .out(adder_1_out), .cout(adder_1_cout));  // open: cin
  // Probe on adder_1_cout
  Multiplexer #(.select(2), .width(4)) multiplexer_1 (
    .in0(adder_1_out), .in1(undriven), .in2(subtractor_1_out), .in3(register_4_q), .out(multiplexer_1_out),
    .sel(or_3_out));
  // Probe on register_2_q
  Subtractor #(.width(4)) subtractor_1 (.a(register_2_q), .b(register_4_q), .out(subtractor_1_out));  // open: bin, bout
  // Probe on nothing

  // Notes on the sheet:
  //   contents of rom_1 (hex, n*v repeats v):
  //   0 16 28 34 43 50 60 70 80 90 a0 b0 c0 d0 e0 f0
endmodule
